// Logisim project colisao_cenario.circ as structural Verilog: 1 circuit, main circuit main
module main (
  input  [31:0] dinozaur,
  input  [31:0] kaktus,
  input  clock,
  input  clock_do_stopu,
  input  stop,
  output [31:0] kolizja,
  output [31:0] obraz
);

  wire and_1_out, and_2_out, and_3_out;
  wire [2:0] counter_2_q;
  wire [4:0] counter_1_q;
  wire [31:0] shifter_1_out;

  and and_1 (and_1_out, clock, ~stop);  // AND_Gate
  Counter #(.width(5), .max('h1f)) counter_1 (
    .Q(counter_1_q), .clk(and_1_out), .clr(and_2_out));  // open: load, D, count, carry
  and and_2 (and_2_out, counter_2_q[2], counter_2_q[1], counter_2_q[0]);
  Counter #(.width(3), .max('h7)) counter_2 (
    .Q(counter_2_q), .clk(and_3_out), .clr(and_2_out));  // open: load, D, count, carry
  and and_3 (and_3_out, clock_do_stopu, stop);
  Shifter #(.width(32)) shifter_1 (.in(kaktus), .\dist (counter_1_q), .out(shifter_1_out));
  assign obraz = dinozaur | shifter_1_out;  // OR_Gate or_1, 32 bits wide
  assign kolizja = dinozaur & shifter_1_out;  // AND_Gate and_4, 32 bits wide
endmodule
