// Logisim project clock_seletor.circ as structural Verilog: 1 circuit, main circuit main
module main (
  input  clock32,
  input  clock64,
  input  clock128,
  input  clock256,
  input  _100,
  input  _1000,
  input  _10000,
  output out
);

  wire and_1_out, and_2_out, and_3_out, and_4_out;

  assign out = and_1_out ? clock32 : 1'bz;  // Controlled_Buffer controlled_buffer_1
  and and_1 (and_1_out, ~_100, ~_1000, ~_10000);  // AND_Gate
  assign out = and_2_out ? clock64 : 1'bz;  // Controlled_Buffer controlled_buffer_2
  and and_2 (and_2_out, _100, ~_1000, ~_10000);  // AND_Gate
  assign out = and_3_out ? clock128 : 1'bz;  // Controlled_Buffer controlled_buffer_3
  and and_3 (and_3_out, ~_100, _1000, ~_10000);  // AND_Gate
  assign out = and_4_out ? clock256 : 1'bz;  // Controlled_Buffer controlled_buffer_4
  and and_4 (and_4_out, ~_100, ~_1000, _10000);  // AND_Gate
endmodule
