// Logisim project obstaculo_tamanho.circ as structural Verilog: 1 circuit, main circuit main
module main (
  input  clock,
  input  in_2,
  input  ptak,
  output \maly_duży 
);

  wire and_1_out, and_2_out, and_3_out, or_1_out;
  wire [5:0] counter_1_q;

  and and_1 (and_1_out, clock, ~ptak);  // AND_Gate
  Counter #(.width(6), .max('h3f)) counter_1 (
    .Q(counter_1_q), .clk(and_2_out), .clr(or_1_out));  // open: load, D, count, carry
  and and_2 (and_2_out, and_1_out, ~in_2);  // AND_Gate
  or or_1 (or_1_out, and_3_out, in_2);
  and and_3 (and_3_out, counter_1_q[1], counter_1_q[2], counter_1_q[5]);
  Random #(.width(1)) random_1 (.clk(and_3_out), .out(\maly_duży ));  // open: next, clr
endmodule
