// Logisim project tela_led.circ as structural Verilog: 1 circuit, main circuit main
module main (
  input  guzik2,
  input  stop,
  input  clock,
  input  guzior,
  output [31:0] kolizja_wiersz_1,
  output [31:0] kolizja_wiersz_2,
  output [31:0] kolizja_wiersz_3,
  output [31:0] kolizja_wiersz_4,
  output [31:0] kolizja_wiersz_5,
  output [31:0] kolizja_wiersz_6,
  output [31:0] kolizja_wiersz_7,
  output [31:0] kolizja_wiersz_8,
  output [31:0] kolizja_wiersz_9,
  output [31:0] kolizja_wiersz_10,
  output [31:0] kolizja_wiersz_11,
  output [31:0] kolizja_wiersz_12,
  output [31:0] kolizja_wiersz_13,
  output [31:0] kolizja_wiersz_14,
  output [31:0] kolizja_wiersz_15,
  output [31:0] out_20,
  output [31:0] out_21,
  output [31:0] out_22,
  output [31:0] out_23,
  output [31:0] out_24,
  output [31:0] out_25,
  output [31:0] out_26,
  output [31:0] out_27,
  output [31:0] out_28,
  output [31:0] out_29,
  output [31:0] out_30,
  output [31:0] out_31,
  output [31:0] out_32,
  output [31:0] out_33,
  output [31:0] out_34,
  output [31:0] out_35,
  output ptak
);

  wire and_2_out, comparator_1_eq, comparator_2_eq, comparator_2_lt, d_ff_1_q, d_ff_1_qn, d_ff_2_q,
       d_ff_2_qn, \main_2_łałanakła , main_3_clock_out, main_4_clock_out, main_5_clock_out, not_1_out,
       not_2_out, not_3_out, not_4_out, not_5_out, or_1_out, xor_1_out;
  wire [1:0] random_1_out;
  wire [31:0] controlled_buffer_6_out, controlled_buffer_7_out, controlled_buffer_8_out,
       controlled_buffer_17_out, controlled_buffer_19_out, controlled_buffer_21_out,
       controlled_buffer_23_out, main_1_dino1, main_1_dino2, main_1_dino3, main_1_dino4, main_1_dino5,
       main_1_dino6, main_1_dino7, main_1_dino8, main_1_dino9, main_1_dino10, main_1_dino11, main_1_dino12,
       main_1_dino13, main_1_dino14, main_1_dino15, main_2_dol, main_2_gora, main_2_out_16, main_2_out_17,
       main_2_out_18, main_3_kaktus_out, main_4_kaktus_out, main_5_kaktus_out, main_7_obraz, main_8_obraz;

  dino_sprite_main main_1 (
    .guzik_1(guzik2), .clock(clock), .stop(stop), .dino15(main_1_dino15), .dino14(main_1_dino14),
    .dino13(main_1_dino13), .dino12(main_1_dino12), .dino11(main_1_dino11), .dino10(main_1_dino10),
    .dino9(main_1_dino9), .dino8(main_1_dino8), .dino7(main_1_dino7), .dino6(main_1_dino6),
    .dino5(main_1_dino5), .dino4(main_1_dino4), .dino3(main_1_dino3), .dino2(main_1_dino2),
    .dino1(main_1_dino1), .dino0(out_35));
  Comparator #(.width(32), .mode("unsigned")) comparator_1 (
    .a(main_2_out_17), .b({32{1'b0}}), .eq(comparator_1_eq));  // open: gt, lt
  Comparator #(.width(32), .mode("unsigned")) comparator_2 (
    .a({32{1'b0}}), .b(controlled_buffer_23_out), .eq(comparator_2_eq), .lt(comparator_2_lt));  // open: gt
  D_Flip_Flop d_ff_1 (
    .clk(comparator_1_eq), .D(d_ff_1_qn), .Q(d_ff_1_q), .Qn(d_ff_1_qn), .reset(xor_1_out));  // open: preset, en
  D_Flip_Flop d_ff_2 (
    .clk(comparator_2_eq), .D(d_ff_2_qn), .Q(d_ff_2_q), .Qn(d_ff_2_qn), .reset(xor_1_out));  // open: preset, en
  xor xor_1 (xor_1_out, d_ff_1_q, d_ff_2_q);
  and and_1 (ptak, random_1_out[0], random_1_out[1]);
  Random #(.width(2), .seed(23456765)) random_1 (.clk(xor_1_out), .out(random_1_out));  // open: next, clr
  passaros_main main_2 (
    .dino_gora(main_1_dino14), .in_2(main_1_dino13), .in_3(main_1_dino12), .in_4(main_1_dino11),
    .dino_dol(main_1_dino10), .clock(clock), .stop(stop), .ptak(ptak), .clock_do_stopu(and_2_out),
    .kolizja_1(kolizja_wiersz_2), .kolizja_2(kolizja_wiersz_3), .kolizja_3(kolizja_wiersz_4),
    .kolizja_4(kolizja_wiersz_5), .kolizja_5(kolizja_wiersz_6), .gora(main_2_gora), .out_16(main_2_out_16),
    .out_17(main_2_out_17), .out_18(main_2_out_18), .dol(main_2_dol), .\łałanakła (\main_2_łałanakła ));
  assign out_21 = stop ? 32'hf3cf3c0 : 32'bz;  // Controlled_Buffer controlled_buffer_1
  assign out_21 = not_1_out ? main_2_gora : 32'bz;  // Controlled_Buffer controlled_buffer_2
  assign out_22 = stop ? 32'h8208240 : 32'bz;  // Controlled_Buffer controlled_buffer_3
  not not_1 (not_1_out, stop);
  assign out_22 = not_1_out ? main_2_out_16 : 32'bz;  // Controlled_Buffer controlled_buffer_4
  assign out_27 = stop ? {32{1'b0}} : 32'bz;  // Controlled_Buffer controlled_buffer_5
  assign controlled_buffer_6_out = not_1_out ? {32{1'b0}} : 32'bz;  // Controlled_Buffer controlled_buffer_6
  assign controlled_buffer_7_out = not_1_out ? {32{1'b0}} : 32'bz;  // Controlled_Buffer controlled_buffer_7
  assign controlled_buffer_8_out = not_1_out ? {32{1'b0}} : 32'bz;  // Controlled_Buffer controlled_buffer_8
  assign controlled_buffer_7_out = stop ? {32{1'b0}} : 32'bz;  // Controlled_Buffer controlled_buffer_9
  and and_2 (and_2_out, clock, ~ptak);  // AND_Gate
  assign out_23 = stop ? 32'he38f240 : 32'bz;  // Controlled_Buffer controlled_buffer_10
  assign out_25 = stop ? 32'h8201240 : 32'bz;  // Controlled_Buffer controlled_buffer_11
  assign out_25 = not_1_out ? main_2_dol : 32'bz;  // Controlled_Buffer controlled_buffer_12
  assign out_26 = stop ? 32'h83cf240 : 32'bz;  // Controlled_Buffer controlled_buffer_13
  assign out_23 = not_1_out ? main_2_out_17 : 32'bz;  // Controlled_Buffer controlled_buffer_14
  assign out_24 = stop ? 32'he38f3c0 : 32'bz;  // Controlled_Buffer controlled_buffer_15
  assign out_24 = not_1_out ? main_2_out_18 : 32'bz;  // Controlled_Buffer controlled_buffer_16
  cacto_sprite_main main_3 (
    .kaktus_0_klatka({32{1'b0}}), .kaktus_1_klatka(32'h1), .kaktus_2_klatka(32'h2), .kaktus_3_klatka(32'h5),
    .kaktus_4klatka(32'ha), .kaktus_5_klatka(32'h15), .clock(and_2_out), .stop(stop),
    .kaktus_out(main_3_kaktus_out), .clock_out(main_3_clock_out));
  or or_1 (or_1_out, \main_2_łałanakła , main_3_clock_out);
  cacto_sprite_main main_4 (
    .kaktus_0_klatka({32{1'b0}}), .kaktus_1_klatka({32{1'b0}}), .kaktus_2_klatka({32{1'b0}}),
    .kaktus_3_klatka(32'h1), .kaktus_4klatka(32'h2), .kaktus_5_klatka(32'h4), .clock(and_2_out), .stop(stop),
    .kaktus_out(main_4_kaktus_out), .clock_out(main_4_clock_out));
  assign controlled_buffer_17_out = guzior ? main_4_kaktus_out : 32'bz;  // Controlled_Buffer controlled_buffer_17
  cacto_sprite_main main_5 (
    .kaktus_0_klatka({32{1'b0}}), .kaktus_1_klatka(32'h1), .kaktus_2_klatka(32'h3), .kaktus_3_klatka(32'h7),
    .kaktus_4klatka(32'hf), .kaktus_5_klatka(32'h1f), .clock(and_2_out), .stop(stop),
    .kaktus_out(main_5_kaktus_out), .clock_out(main_5_clock_out));
  not not_2 (not_2_out, guzior);
  assign controlled_buffer_17_out = not_3_out ? main_3_kaktus_out : 32'bz;  // Controlled_Buffer controlled_buffer_18
  not not_3 (not_3_out, guzior);
  assign controlled_buffer_19_out = guzior ? main_3_kaktus_out : 32'bz;  // Controlled_Buffer controlled_buffer_19
  assign controlled_buffer_19_out = not_4_out ? main_5_kaktus_out : 32'bz;  // Controlled_Buffer controlled_buffer_20
  not not_4 (not_4_out, guzior);
  assign controlled_buffer_21_out = guzior ? {32{1'b0}} : 32'bz;  // Controlled_Buffer controlled_buffer_21
  assign controlled_buffer_21_out = not_2_out ? main_4_kaktus_out : 32'bz;  // Controlled_Buffer controlled_buffer_22
  assign controlled_buffer_23_out = guzior ? main_5_kaktus_out : 32'bz;  // Controlled_Buffer controlled_buffer_23
  assign controlled_buffer_23_out = not_5_out ? main_4_kaktus_out : 32'bz;  // Controlled_Buffer controlled_buffer_24
  not not_5 (not_5_out, guzior);
  colisao_cenario_main main_6 (
    .dinozaur(main_1_dino15), .kaktus({32{1'b0}}), .clock(stop), .clock_do_stopu(and_2_out), .stop(stop),
    .kolizja(kolizja_wiersz_1), .obraz(out_20));
  colisao_cenario_main main_7 (
    .dinozaur(main_1_dino9), .kaktus(controlled_buffer_8_out), .clock(or_1_out), .clock_do_stopu(and_2_out),
    .stop(stop), .kolizja(kolizja_wiersz_7), .obraz(main_7_obraz));
  colisao_cenario_main main_8 (
    .dinozaur(main_1_dino8), .kaktus(controlled_buffer_6_out), .clock(or_1_out), .clock_do_stopu(and_2_out),
    .stop(stop), .kolizja(kolizja_wiersz_8), .obraz(main_8_obraz));
  colisao_cenario_main main_9 (
    .dinozaur(main_1_dino7), .kaktus(controlled_buffer_7_out), .clock(or_1_out), .clock_do_stopu(and_2_out),
    .stop(stop), .kolizja(kolizja_wiersz_9), .obraz(out_28));
  colisao_cenario_main main_10 (
    .dinozaur(main_1_dino6), .kaktus({32{1'b0}}), .clock(or_1_out), .clock_do_stopu(and_2_out), .stop(stop),
    .kolizja(kolizja_wiersz_10), .obraz(out_29));
  colisao_cenario_main main_11 (
    .dinozaur(main_1_dino5), .kaktus(controlled_buffer_21_out), .clock(or_1_out), .clock_do_stopu(and_2_out),
    .stop(stop), .kolizja(kolizja_wiersz_11), .obraz(out_30));
  colisao_cenario_main main_12 (
    .dinozaur(main_1_dino4), .kaktus(controlled_buffer_17_out), .clock(or_1_out), .clock_do_stopu(and_2_out),
    .stop(stop), .kolizja(kolizja_wiersz_12), .obraz(out_31));
  colisao_cenario_main main_13 (
    .dinozaur(main_1_dino3), .kaktus(controlled_buffer_19_out), .clock(or_1_out), .clock_do_stopu(and_2_out),
    .stop(stop), .kolizja(kolizja_wiersz_13), .obraz(out_32));
  colisao_cenario_main main_14 (
    .dinozaur(main_1_dino2), .kaktus(controlled_buffer_23_out), .clock(or_1_out), .clock_do_stopu(and_2_out),
    .stop(stop), .kolizja(kolizja_wiersz_14), .obraz(out_33));
  colisao_cenario_main main_15 (
    .dinozaur(main_1_dino1), .kaktus(main_4_kaktus_out), .clock(or_1_out), .clock_do_stopu(and_2_out),
    .stop(stop), .kolizja(kolizja_wiersz_15), .obraz(out_34));
  assign out_26 = not_1_out ? main_7_obraz : 32'bz;  // Controlled_Buffer controlled_buffer_25
  assign out_27 = not_1_out ? main_8_obraz : 32'bz;  // Controlled_Buffer controlled_buffer_26
endmodule
